// Logisim project tinycpu_2.circ as structural Verilog: 3 circuits, main circuit main
module main (
  input  in_1,
  input  [15:0] in_2,
  input  in_3,
  input  in_4,
  input  in_5,
  input  in_6,
  input  in_7,
  input  in_8,
  input  in_9,
  input  in_10,
  input  in_11,
  input  in_12,
  input  in_13,
  input  in_14,
  input  in_15,
  output [15:0] out_16,
  output [15:0] out_17,
  output [15:0] out_18,
  output [15:0] out_19,
  output [15:0] out_20,
  output [11:0] out_21,
  output [15:0] out_22,
  output [11:0] out_23,
  output [3:0] out_24,
  output [11:0] out_25,
  output [15:0] out_26,
  output [15:0] out_27,
  output [2:0] out_28,
  output [11:0] out_29
);

  wire A_WE, ALU_SEL, ALU_SUB, B_WE, C_WE, clk, clock_1_out, IS_A_EQ_B, IS_A_REG_ZERO, MAR_WE,
       MEM_HI_REG_RST, not_1_out, PC_WE, RAM_WE, STEP_REG_RST;
  wire [3:0] bit_extender_1_out, STEP_PLUS_1;
  wire [7:0] RAM_IN;
  wire [11:0] bit_extender_3_out, bit_extender_4_out, MAR_IN, MAR_PLUS_1, PC_IN, PC_PLUS_1;
  wire [15:0] C_REG, INST_ADDR_EXT, MUL_OUT, PC_REG_EXT, SUM_OUT;
  wire [31:3] CONTROL;

  Clock clock_1 (.out(clock_1_out));
  not not_1 (not_1_out, CONTROL[15]);
  and and_1 (clk, clock_1_out, not_1_out);
  Register REG_MEM_HI (.D(out_20[7:0]), .en(CONTROL[17]), .clk(clk), .Q(out_20[15:8]), .clr(MEM_HI_REG_RST));
  or or_1 (STEP_REG_RST, in_1, CONTROL[14]);
  Register #(.width(16)) REG_A (.D(out_26), .en(A_WE), .clk(clk), .Q(out_16), .clr(in_1));
  Register #(.width(16)) REG_B (.D(out_26), .en(B_WE), .clk(clk), .Q(out_18), .clr(in_1));
  Register #(.width(12)) REG_PC (.D(PC_IN), .en(PC_WE), .clk(clk), .Q(out_21), .clr(in_1));
  Register #(.width(12)) REG_MAR (.D(MAR_IN), .en(MAR_WE), .clk(clk), .Q(out_23), .clr(in_1));
  Register REG_INST_MSB (.D(out_26[7:0]), .en(CONTROL[9]), .clk(clk), .Q(out_22[15:8]), .clr(in_1));
  Register REG_INST_LSB (.D(out_26[7:0]), .en(CONTROL[10]), .clk(clk), .Q(out_22[7:0]), .clr(in_1));
  Register #(.width(4)) REG_STEP (.D(STEP_PLUS_1), .en(1'b1), .clk(clk), .Q(out_24), .clr(STEP_REG_RST));
  RAM #(.addrWidth(12), .asyncread("true")) ram_1 (
    .addr(out_23), .we(RAM_WE), .oe(1'b1), .clk(clk), .din(RAM_IN), .dout(out_20[7:0]));
  assign bit_extender_1_out = {{3{1'b0}}, 1'b1};  // Bit_Extender bit_extender_1
  assign PC_REG_EXT = {{4{1'b0}}, out_21};  // Bit_Extender bit_extender_2
  or or_2 (MEM_HI_REG_RST, in_1, CONTROL[18]);
  Adder #(.width(4)) adder_1 (.a(out_24), .b(bit_extender_1_out), .out(STEP_PLUS_1), .cin(1'b0));  // open: cout
  Multiplexer #(.select(3), .width(16)) multiplexer_1 (
    .in0(out_16), .in1(out_18), .in2(C_REG), .in3(out_19), .in4(out_20), .in5(PC_REG_EXT),
    .in6(INST_ADDR_EXT), .in7(in_2), .out(out_26), .sel(out_28));
  assign bit_extender_3_out = {{11{1'b0}}, 1'b1};  // Bit_Extender bit_extender_3
  assign bit_extender_4_out = {{11{1'b0}}, 1'b1};  // Bit_Extender bit_extender_4
  Adder #(.width(12)) adder_2 (.a(out_21), .b(bit_extender_3_out), .out(PC_PLUS_1), .cin(1'b0));  // open: cout
  or or_3 (PC_WE, CONTROL[7], CONTROL[8]);
  Multiplexer #(.select(2), .width(12)) multiplexer_2 (
    .in1(PC_PLUS_1), .in2(out_26[11:0]), .out(PC_IN), .sel(CONTROL[8:7]));  // open: in0, in3
  Adder #(.width(12)) adder_3 (.a(out_23), .b(bit_extender_4_out), .out(MAR_PLUS_1), .cin(1'b0));  // open: cout
  or or_4 (MAR_WE, CONTROL[3], CONTROL[4]);
  assign INST_ADDR_EXT = {{4{1'b0}}, out_22[11:0]};  // Bit_Extender bit_extender_5
  or or_5 (RAM_WE, CONTROL[5], CONTROL[6]);
  ROM #(.addrWidth(12), .dataWidth(32)) rom_1 (
    .addr({out_22[15:12], out_24, out_25[3:0]}),
    .data({CONTROL[31:20], ALU_SEL, CONTROL[18:17], ALU_SUB, CONTROL[15:14], out_28, CONTROL[10:3], C_WE, B_WE, A_WE}));
  Multiplexer #(.select(2), .width(12)) multiplexer_3 (
    .in1(MAR_PLUS_1), .in2(out_26[11:0]), .out(MAR_IN), .sel({CONTROL[3], CONTROL[4]}));  // open: in0, in3
  Multiplexer #(.select(2), .width(8)) multiplexer_4 (
    .in1(out_26[15:8]), .in2(out_26[7:0]), .out(RAM_IN), .sel(CONTROL[6:5]));  // open: in0, in3
  Adder #(.width(16)) adder_4 (.a(out_16), .b(out_18), .out(SUM_OUT), .cin(1'b0));  // open: cout
  Multiplier #(.width(16)) multiplier_1 (.a(out_16), .b(out_18), .out(MUL_OUT), .cin({16{1'b0}}));  // open: cout
  Comparator #(.mode("unsigned"), .width(16)) comparator_1 (.a(out_16), .b(out_18), .eq(IS_A_EQ_B));  // open: gt, lt
  Multiplexer #(.width(16)) multiplexer_5 (.in0(SUM_OUT), .in1(MUL_OUT), .out(out_19), .sel(ALU_SEL));
  nor nor_1 (IS_A_REG_ZERO, out_16[0], out_16[1], out_16[2], out_16[3], out_16[4], out_16[5], out_16[6], out_16[7], out_16[8], out_16[9], out_16[10], out_16[11], out_16[12], out_16[13], out_16[14], out_16[15]);
  assign out_25[3:0] = {{2{1'b0}}, {IS_A_EQ_B, IS_A_REG_ZERO}};  // Bit_Extender bit_extender_6

  assign out_17 = out_16;
  assign out_25[11:4] = {out_22[15:12], out_24};
  assign out_27 = out_26;
  assign out_29 = {out_22[15:12], out_24, out_25[3:0]};

  // Other names for the same wires on the sheet: PC_INC = CONTROL[7]; PC_JMP = CONTROL[8]; MAR_INC = CONTROL[4];
  //   MAR_BUS_WE = CONTROL[3]; RAM_MSB_WE = CONTROL[5]; RAM_LSB_WE = CONTROL[6]; A_REG[15:0] = out_16;
  //   ALU_OUT[15:0] = out_19; ALU_SEL_0 = ALU_SEL; CONTROL (some bits) = {ALU_SEL, ALU_SUB, out_28, C_WE, B_WE, A_WE};
  //   B_REG[15:0] = out_18; BUS_0_3[3:0] = out_26[3:0]; BUS_0_11[11:0] = out_26[11:0]; BUS_LSB[7:0] = out_26[7:0];
  //   THE_BUS[15:0] = out_26; BUS_4_7[3:0] = out_26[7:4]; BUS_8_11[3:0] = out_26[11:8]; BUS_MSB[7:0] = out_26[15:8];
  //   BUS_12_15[3:0] = out_26[15:12]; INST_MSB_WE = CONTROL[9]; INST_LSB_WE = CONTROL[10];
  //   INST_STEP_RST = CONTROL[14]; HLT = CONTROL[15]; MEM_HI_WE = CONTROL[17]; MEM_HI_RST = CONTROL[18];
  //   INST_ADDR[11:0] = out_22[11:0]; INST_LSB_REG[7:0] = out_22[7:0]; INST_REG[15:0] = out_22;
  //   INST_REG_0_3[3:0] = out_22[3:0]; INST_REG_4_7[3:0] = out_22[7:4]; INST_MSB_REG[7:0] = out_22[15:8];
  //   INST_REG_8_11[3:0] = out_22[11:8]; MAN_REG[15:0] = in_2; MAR_REG[11:0] = out_23; PC_REG[11:0] = out_21;
  //   RAM_REG[7:0] = out_20[7:0]; RAM_REG_EXT[15:0] = out_20; MEM_HI_REG[7:0] = out_20[15:8]; BUS_SRC_0 = out_28[0];
  //   REG_SEL[2:0] = out_28; BUS_SRC_1 = out_28[1]; BUS_SRC_2 = out_28[2]; COND_FLAGS[3:0] = out_25[3:0];
  //   ROM_LOOKUP[11:0] = {out_22[15:12], out_24, out_25[3:0]}; STEP_REG[3:0] = out_24;
  //   INST_OPCODE[3:0] = out_22[15:12]; RST = in_1

  // Notes on the sheet:
  //   contents of rom_1 (hex, n*v repeats v):
  //   16*2808 16*2200 16*80 16*2808 16*2480 16*4000 160*0 16*2808 16*2200 16*80 16*2808 16*2480 16*3008
  //   16*20000 16*10 16*2001 16*4000 96*0 16*2808 16*2200 16*80 16*2808 16*2480 16*3008 16*20000 16*10
  //   16*2002 16*1801 16*4000 80*0 16*2808 16*2200 16*80 16*2808 16*2480 16*4000 160*0 16*2808 16*2200
  //   16*80 16*2808 16*2480 16*3008 16*20 16*10 16*40 16*4000 96*0 16*2808 16*2200 16*80 16*2808 16*2480
  //   16*3001 16*4000 144*0 16*2808 16*2200 16*80 16*2808 16*2480 16*3100 16*4000 144*0 16*2808 16*2200
  //   16*80 16*2808 16*2480 4000 3100 4000 3100 4000 3100 4000 3100 4000 3100 4000 3100 4000 3100 4000
  //   3100 17*4000 0 4000 0 4000 0 4000 0 4000 0 4000 0 4000 0 4000 0 4000 0 4000 0 4000 0 4000 0 4000 0
  //   4000 0 4000 0 4000 0 4000 0 4000 0 4000 0 4000 0 4000 0 4000 0 4000 0 4000 0 4000 0 4000 0 4000 0
  //   4000 0 4000 0 4000 0 4000 0 4000 0 4000 0 4000 0 4000 0 4000 0 4000 0 4000 0 4000 0 4000 0 4000 0
  //   4000 0 4000 0 4000 0 4000 0 4000 0 4000 0 4000 0 4000 0 4000 0 4000 0 4000 0 4000 0 4000 0 4000 0
  //   4000 0 4000 0 4000 0 4000 0 4000 0 4000 0 4000 0 4000 0 4000 0 4000 0 4000 0 4000 0 4000 0 4000 0
  //   4000 0 4000 0 4000 0 16*2808 16*2200 16*80 16*2808 16*2480 16*3008 16*20000 16*10 16*2002 16*81801
  //   96*0 16*2808 16*2200 16*80 16*2808 16*2480 16*3008 16*20000 16*10 16*2002 16*4000 96*0 16*2808
  //   16*2200 16*80 16*2808 16*2480 4000 4000 3100 3100 4000 4000 3100 3100 4000 4000 3100 3100 4000 4000
  //   3100 3100 18*4000 0 0 4000 4000 0 0 4000 4000 0 0 4000 4000 0 0 4000 4000 0 0 4000 4000 0 0 4000
  //   4000 0 0 4000 4000 0 0 4000 4000 0 0 4000 4000 0 0 4000 4000 0 0 4000 4000 0 0 4000 4000 0 0 4000
  //   4000 0 0 4000 4000 0 0 4000 4000 0 0 4000 4000 0 0 4000 4000 0 0 4000 4000 0 0 4000 4000 0 0 4000
  //   4000 0 0 4000 4000 0 0 4000 4000 0 0 4000 4000 0 0 4000 4000 0 0 4000 4000 0 0 4000 4000 0 0 4000
  //   4000 0 0 4000 4000 0 0 4000 4000 0 0 4000 4000 0 0 4000 4000 0 0 4000 4000 0 0 4000 4000 0 0 4000
  //   4000 0 0 4000 4000 0 0 16*2808 16*2200 16*80 16*2808 16*2480 176*0 16*2808 16*2200 16*80 16*2808
  //   16*2480 176*0 16*2808 16*2200 16*80 16*2808 16*2480 176*0 16*2808 16*2200 16*80 16*2808 16*2480
  //   176*0 16*2808 16*2200 16*80 16*2808 16*2480 16*8000
endmodule

module mul (
  input  [7:0] in_1,
  input  [3:0] in_2,
  input  [3:0] in_3,
  input  in_4,
  output [7:0] out_5,
  output [7:0] out_6,
  output [7:0] out_7,
  output [7:0] out_8,
  output [3:0] out_9,
  output [3:0] out_10,
  output [3:0] out_11,
  output [3:0] out_12,
  output [7:0] out_13,
  output [7:0] out_14,
  output [7:0] out_15,
  output [7:0] out_16
);

  wire a1, a2, a3, a4, clk;
  wire [3:0] P1;
  wire [4:1] P2;
  wire [5:2] P3;
  wire [6:3] P4;
  wire [7:0] M_gated, P_IN, S1, S2;

  assign out_6 = {{4{1'b0}}, in_2};  // Bit_Extender bit_extender_1
  and and_1 (P1[0], a1, in_3[0]);
  and and_2 (P1[1], a2, in_3[0]);
  and and_3 (P1[2], a3, in_3[0]);
  and and_4 (P1[3], a4, in_3[0]);
  Multiplexer #(.width(8)) multiplexer_1 (.in0({out_8[6:0], 1'b0}), .in1(out_6), .out(out_7), .sel(in_4));
  and and_5 (P2[1], a1, in_3[1]);
  and and_6 (P2[2], a2, in_3[1]);
  and and_7 (P2[3], a3, in_3[1]);
  and and_8 (P2[4], a4, in_3[1]);
  Register register_1 (.D(out_7), .en(1'b1), .clk(clk), .Q(out_8));  // open: clr
  Adder adder_1 (.a({4'b0000, P1}), .b({3'b000, P2, 1'b0}), .out(S1), .cin(1'b0));  // open: cout
  Adder adder_2 (.a(S1), .b(S2), .out(out_5), .cin(1'b0));  // open: cout
  Adder adder_3 (.a({2'b00, P3, 2'b00}), .b({1'b0, P4, 3'b000}), .out(S2), .cin(1'b0));  // open: cout
  Clock clock_1 (.out(clk));
  and and_9 (P3[2], a1, in_3[2]);
  and and_10 (P3[3], a2, in_3[2]);
  and and_11 (P3[4], a3, in_3[2]);
  and and_12 (P3[5], a4, in_3[2]);
  Multiplexer #(.width(4)) multiplexer_2 (.in0({1'b0, out_11[2:0]}), .in1(in_3), .out(out_10), .sel(in_4));
  assign out_16 = {{7{out_12[0]}}, out_12[0]};  // Bit_Extender bit_extender_2
  Register #(.width(4)) register_2 (.D(out_10), .en(1'b1), .clk(clk), .Q({out_11[2:0], out_12[0]}));  // open: clr
  and and_13 (P4[3], a1, in_3[3]);
  and and_14 (P4[4], a2, in_3[3]);
  and and_15 (P4[5], a3, in_3[3]);
  and and_16 (P4[6], a4, in_3[3]);
  Adder adder_4 (.a(out_13), .b(M_gated), .out(out_15));  // open: cin, cout
  Multiplexer #(.width(8)) multiplexer_3 (.in0(out_15), .in1({8{1'b0}}), .out(P_IN), .sel(in_4));
  assign M_gated = out_8 & out_16;  // AND_Gate and_17, 8 bits wide
  Register register_3 (.D(P_IN), .en(1'b1), .clk(clk), .Q(out_13));  // open: clr

  assign out_9 = in_3;
  assign out_11[3] = 1'b0;
  assign out_12[3:1] = out_11[2:0];
  assign out_14 = out_13;

  // Other names for the same wires on the sheet: A[3:0] = in_2; B[3:0] = in_3; b1 = in_3[0]; b2 = in_3[1];
  //   b3 = in_3[2]; b4 = in_3[3]; LOAD_MUL = in_4; M[7:0] = out_8; m1 = out_8[0]; M_SHIFT[7:1] = out_8[6:0];
  //   m2 = out_8[1]; m3 = out_8[2]; m4 = out_8[3]; m5 = out_8[4]; m6 = out_8[5]; m7 = out_8[6]; m8 = out_8[7];
  //   M0[7:0] = out_6; M_IN[7:0] = out_7; P[7:0] = out_13; P_PLUS_M[7:0] = out_15; Q[3:0] = {out_11[2:0], out_12[0]};
  //   q1 = out_12[0]; q2 = out_11[0]; Q_shift[2:0] = out_11[2:0]; q3 = out_11[1]; q4 = out_11[2];
  //   q1_fanout[7:0] = out_16; Q_in[3:0] = out_10; S3[7:0] = out_5
endmodule

module cmp (
  input  in_1,
  input  in_2,
  input  in_3,
  input  in_4,
  input  in_5,
  input  in_6,
  input  in_7,
  input  in_8,
  input  in_9,
  input  in_10
);

  wire and_1_out, not_1_out, not_2_out, not_3_out, not_4_out, not_5_out, xor_1_out, xor_2_out, xor_3_out,
       xor_4_out, xor_5_out;

  xor xor_1 (xor_1_out, in_1, in_2);
  not not_1 (not_1_out, xor_1_out);
  xor xor_2 (xor_2_out, in_3, in_4);
  not not_2 (not_2_out, xor_2_out);
  xor xor_3 (xor_3_out, in_5, in_6);
  not not_3 (not_3_out, xor_3_out);
  xor xor_4 (xor_4_out, in_7, in_8);
  not not_4 (not_4_out, xor_4_out);
  xor xor_5 (xor_5_out, in_9, in_10);
  not not_5 (not_5_out, xor_5_out);
  and and_1 (and_1_out, not_1_out, not_2_out, not_3_out, not_4_out, not_5_out);
endmodule
